# Fritzing sketch Rodney (saved by Fritzing 0.9.3b)
breadboards: 1

parts:
  ThunderBorg = IC, SIP package, 12 pins [chip_label=IC]
  Raspberry_Pi_1 = Raspberry Pi 3 [part_number=RPI-3-V1.2]
  12V = Screw terminal - 2 pins [package=THT]
  S1 = Taiway 100-SP-X-T1 SPDT Miniature Toggle Switch [part_number=100-SP-X-T1-0-0-B1-M1 package=THT]

nets:
  3V3: ThunderBorg.pin1, Raspberry_Pi_1.3v3, Raspberry_Pi_1.3V3
  N1: ThunderBorg.pin2, Raspberry_Pi_1.5V
  N2: ThunderBorg.pin3, Raspberry_Pi_1.GPIO2
  N3: ThunderBorg.pin5, Raspberry_Pi_1.GPIO3
  N4: ThunderBorg.pin6, Raspberry_Pi_1.GND
  N5: ThunderBorg.pin9, 12V.pin2
  N6: ThunderBorg.pin10, S1.COM
  N7: 12V.pin1, S1.L2
